# Fritzing sketch Consegna1 (saved by Fritzing 0.9.3b)
breadboards: 1

parts:
  Componente1 = Arduino Uno (Rev3)
  LED1 = smd LED [color="Green (565nm)" package="0805 [SMD]"]
  R1 = Resistor [tolerance=±5% resistance=220 package=THT]
  LED2 = smd LED [color="Green (565nm)" package="0805 [SMD]"]
  LED3 = smd LED [color="Green (565nm)" package="0805 [SMD]"]
  R2 = Resistor [tolerance=±5% resistance=220 package=THT]
  R3 = Resistor [tolerance=±5% resistance=220 package=THT]
  R4 = Resistor [tolerance=±5% resistance=10k package=THT]
  S1 = Pushbutton [package="[THT]"]
  S2 = Pushbutton [package="[THT]"]
  S3 = Pushbutton [package="[THT]"]
  R5 = Resistor [tolerance=±5% resistance=10k package=THT]
  R6 = Resistor [tolerance=±5% resistance=10k package=THT]
  R7 = Rotary Potentiometer (Small) [maximum_resistance=100kΩ package=THT]
  LED4 = LED - 5mm [color="Red (633nm)" package="5 mm [THT]"]
  R8 = Resistor [tolerance=±5% resistance=220 package=THT]

nets:
  N1: Componente1.A0, R7.wiper
  N2: Componente1.D9_PWM, R8.Pin_0
  N3: Componente1.D10_PWM/SS, R3.Pin_0
  N4: Componente1.D11_PWM/MOSI, R1.Pin_0
  N5: Componente1.D12/MISO, R2.Pin_0
  N6: Componente1.D2, S3.Pin_1, S3.Pin_2, R6.Pin_1
  N7: Componente1.D3_PWM, S2.Pin_1, S2.Pin_2, R5.Pin_1
  N8: Componente1.D4, R4.Pin_1, S1.Pin_1, S1.Pin_2
  N9: Componente1.5V, S1.Pin_3, S1.Pin_4, S2.Pin_3, S2.Pin_4, S3.Pin_3, S3.Pin_4, R7.leg1
  N10: Componente1.GND, LED1.cathode, LED2.cathode, LED3.cathode, R4.Pin_0, R5.Pin_0, R6.Pin_0, R7.leg2, LED4.cathode
  N11: LED1.anode, R1.Pin_1
  N12: LED2.anode, R2.Pin_1
  N13: LED3.anode, R3.Pin_1
  N14: LED4.anode, R8.Pin_1
